# Fritzing sketch GarageSensor (saved by Fritzing 0.9.4)
breadboards: 1

parts:
  8x8_LED_matrix_MAX5 = 8x8 Red 8x8 LED Matrix with MAX7219
  8x8_LED_matrix_MAX6 = 8x8 Red 8x8 LED Matrix with MAX7219
  8x8_LED_matrix_MAX7 = 8x8 Red 8x8 LED Matrix with MAX7219
  8x8_LED_matrix_MAX8 = 8x8 Red 8x8 LED Matrix with MAX7219
  Part2 = Arduino Nano (Rev3.0)
  HC-SR04_Sensor_4 = HC-SR04 Ultrasonic Distance Sensor
  J4 = Piezo Speaker
  H4 = polarizedheader 4pin 0.156in [package=THT]
  R10 = Resistor [tolerance=±5% resistance=4.7k package="1206 [SMD]"]
  R11 = PHOTOCELL [package=photocell]
  R12 = Resistor [tolerance=±5% resistance=1k package="2512 [SMD]"]
  S4 = SWITCH-MOMENTARY-2 [package=tactile-pth]

nets:
  VCC: 8x8_LED_matrix_MAX5.VCC, 8x8_LED_matrix_MAX5.VCC_PT, 8x8_LED_matrix_MAX6.VCC, 8x8_LED_matrix_MAX6.VCC_PT, 8x8_LED_matrix_MAX7.VCC, 8x8_LED_matrix_MAX7.VCC_PT, 8x8_LED_matrix_MAX8.VCC, 8x8_LED_matrix_MAX8.VCC_PT, Part2.5V, HC-SR04_Sensor_4.VCC, H4.pin1, R10.Pin_0, R11.P$1
  GND: 8x8_LED_matrix_MAX5.GND, 8x8_LED_matrix_MAX5.CLK_PT, 8x8_LED_matrix_MAX6.GND_PT, 8x8_LED_matrix_MAX6.CLK, 8x8_LED_matrix_MAX7.GND, 8x8_LED_matrix_MAX7.CLK_PT, 8x8_LED_matrix_MAX8.GND_PT, 8x8_LED_matrix_MAX8.CLK, Part2.D13/SCK
  GND_2: 8x8_LED_matrix_MAX5.GND_PT, 8x8_LED_matrix_MAX5.CLK, 8x8_LED_matrix_MAX6.GND, 8x8_LED_matrix_MAX6.CLK_PT, 8x8_LED_matrix_MAX7.GND_PT, 8x8_LED_matrix_MAX7.CLK, 8x8_LED_matrix_MAX8.GND, 8x8_LED_matrix_MAX8.CLK_PT, Part2.GND, HC-SR04_Sensor_4.GND, H4.pin4, R12.Pin_1, S4.1
  N1: 8x8_LED_matrix_MAX5.DIN, 8x8_LED_matrix_MAX6.DIN_CHN, 8x8_LED_matrix_MAX6.CS, 8x8_LED_matrix_MAX7.CS_PT
  N2: 8x8_LED_matrix_MAX5.DIN_CHN, 8x8_LED_matrix_MAX5.CS, 8x8_LED_matrix_MAX6.CS_PT
  N3: 8x8_LED_matrix_MAX6.DIN, 8x8_LED_matrix_MAX7.DIN_CHN, 8x8_LED_matrix_MAX7.CS, 8x8_LED_matrix_MAX8.CS_PT
  N4: 8x8_LED_matrix_MAX7.DIN, 8x8_LED_matrix_MAX8.DIN_CHN, 8x8_LED_matrix_MAX8.CS, Part2.D9
  N5: 8x8_LED_matrix_MAX8.DIN, Part2.D10
  N6: Part2.D2, H4.pin2, R10.Pin_1
  N7: Part2.D5, J4.pin2
  N8: Part2.D6, HC-SR04_Sensor_4.TRIG
  N9: Part2.D7, HC-SR04_Sensor_4.ECHO
  N10: Part2.D8, S4.2
  N11: Part2.A0, R11.P$2, R12.Pin_0

notes:
  32x8 Led Matrix for max7219 controller
  Buzzer
  HC-SR04
  Arduino - Eg. Nano
  DHT - 22
  Resistor 1K
  Photoresistor
  Resistor 4.7K
  Button

custom parts:
  8x8 Red 8x8 LED Matrix with MAX7219: Description: 8 by 8 red LED matrix with a MAX7219 controller.
